// Logisim project Lab1.circ as structural Verilog: 6 circuits, main circuit P3
module P3 (
  input  NOT,
  input  XOR,
  input  in_3,
  input  AND,
  input  in_5,
  input  XNOR,
  input  OR,
  input  in_8,
  input  in_9,
  output out_10,
  output out_11,
  output out_12,
  output out_13,
  output out_14
);

  wire nand_1_out, nand_2_out, nand_3_out, nand_7_out, nand_8_out, nand_9_out, nand_10_out, nand_11_out,
       nand_12_out, nand_13_out;

  nand nand_1 (nand_1_out, AND, in_5);
  nand nand_2 (nand_2_out, OR, OR);
  nand nand_3 (nand_3_out, in_8, in_8);
  nand nand_4 (out_10, NOT, NOT);
  nand nand_5 (out_13, nand_2_out, nand_3_out);
  nand nand_6 (out_12, nand_1_out, nand_1_out);
  nand nand_7 (nand_7_out, XNOR, in_9);
  nand nand_8 (nand_8_out, XOR, in_3);
  not nand_9 (nand_9_out, nand_7_out);  // NAND_Gate
  not nand_10 (nand_10_out, nand_7_out);  // NAND_Gate
  not nand_11 (nand_11_out, nand_8_out);  // NAND_Gate
  not nand_12 (nand_12_out, nand_8_out);  // NAND_Gate
  nand nand_13 (nand_13_out, nand_9_out, nand_10_out);
  nand nand_14 (out_11, nand_11_out, nand_12_out);
  not nand_15 (out_14, nand_13_out);  // NAND_Gate
endmodule

module P4 (
  input  NOT,
  input  AND,
  input  in_3,
  input  OR,
  input  in_5,
  input  XOR,
  input  in_7,
  output out_8,
  output out_9,
  output out_10,
  output out_11
);

  wire nor_1_out, nor_4_out, nor_5_out, nor_6_out, nor_7_out, nor_9_out, nor_10_out;

  nor nor_1 (nor_1_out, OR, in_5);
  nor nor_2 (out_8, NOT, NOT);
  nor nor_3 (out_10, nor_1_out, nor_1_out);
  nor nor_4 (nor_4_out, XOR, in_7);
  nor nor_5 (nor_5_out, XOR, nor_4_out);
  nor nor_6 (nor_6_out, nor_4_out, in_7);
  nor nor_7 (nor_7_out, nor_5_out, nor_6_out);
  nor nor_8 (out_11, nor_7_out, nor_7_out);
  nor nor_9 (nor_9_out, AND, AND);
  nor nor_10 (nor_10_out, in_3, in_3);
  nor nor_11 (out_9, nor_9_out, nor_10_out);
endmodule

module P5 (
  input  in_1,
  input  in_2,
  input  in_3,
  input  in_4,
  output out_5
);

  wire n7400_1_pin1, n7400_1_pin3, n7400_1_pin5, n7400_1_pin6, n7400_2_pin1, n7400_2_pin3, n7400_2_pin5,
       n7400_2_pin12, n7400_3_pin1, n7400_3_pin3, n7400_3_pin5;

  _7400 #(.ShowInternalStructure("true")) u_7400_1 (
    .pin1(n7400_1_pin1), .pin2(in_1), .pin3(n7400_1_pin3), .pin4(n7400_1_pin3), .pin5(n7400_1_pin5),
    .pin6(n7400_1_pin6), .pin13(in_1), .pin12(in_2), .pin11(n7400_1_pin1), .pin10(n7400_1_pin1), .pin9(in_2),
    .pin8(n7400_1_pin5));
  _7400 #(.ShowInternalStructure("true")) u_7400_2 (
    .pin1(n7400_2_pin1), .pin2(n7400_1_pin6), .pin3(n7400_2_pin3), .pin4(n7400_2_pin3), .pin5(n7400_2_pin5),
    .pin6(out_5), .pin13(n7400_1_pin6), .pin12(n7400_2_pin12), .pin11(n7400_2_pin1), .pin10(n7400_2_pin1),
    .pin9(n7400_2_pin12), .pin8(n7400_2_pin5));
  _7400 #(.ShowInternalStructure("true")) u_7400_3 (
    .pin1(n7400_3_pin1), .pin2(in_3), .pin3(n7400_3_pin3), .pin4(n7400_3_pin3), .pin5(n7400_3_pin5),
    .pin6(n7400_2_pin12), .pin13(in_3), .pin12(in_4), .pin11(n7400_3_pin1), .pin10(n7400_3_pin1),
    .pin9(in_4), .pin8(n7400_3_pin5));

  // Notes on the sheet:
  //   A
  //   B
  //   C
  //   D
endmodule

module P6 (
  input  in_1,
  input  in_2,
  input  in_3,
  input  in_4,
  output out_5
);

  wire nand_1_out, nand_2_out, nand_3_out, nand_4_out, nand_5_out, nand_6_out, nand_7_out, nand_8_out,
       nand_9_out, nand_10_out, nand_11_out, nand_12_out;

  nand nand_1 (nand_1_out, in_2, in_2);
  nand nand_2 (nand_2_out, in_3, in_3);
  nand nand_3 (nand_3_out, in_4, in_4);
  nand nand_4 (nand_4_out, in_4, in_3);
  nand nand_5 (nand_5_out, in_4, in_2);
  nand nand_6 (nand_6_out, nand_2_out, nand_1_out);
  nand nand_7 (nand_7_out, nand_5_out, nand_5_out);
  nand nand_8 (nand_8_out, nand_6_out, nand_6_out);
  nand nand_9 (nand_9_out, nand_2_out, nand_7_out);
  nand nand_10 (nand_10_out, nand_3_out, nand_8_out);
  nand nand_11 (nand_11_out, nand_4_out, nand_9_out);
  nand nand_12 (nand_12_out, nand_11_out, nand_11_out);
  nand nand_13 (out_5, nand_12_out, nand_10_out);

  // Notes on the sheet:
  //   A
  //   B
  //   C
  //   D
endmodule

module P7 (
  input  in_1,
  input  in_2,
  input  in_3,
  input  in_4,
  input  in_5,
  input  in_6,
  input  in_7,
  input  in_8,
  input  Clk,
  output out_10
);

  wire and_1_out, and_2_out, and_3_out, and_4_out, and_5_out, and_6_out, and_7_out, not_1_out, not_2_out,
       not_3_out, not_4_out, not_5_out, not_6_out;

  not not_1 (not_1_out, in_1);
  not not_2 (not_2_out, in_2);
  not not_3 (not_3_out, in_4);
  not not_4 (not_4_out, in_6);
  not not_5 (not_5_out, in_7);
  not not_6 (not_6_out, in_8);
  and and_1 (and_1_out, not_1_out, not_2_out);
  and and_2 (and_2_out, in_3, not_3_out);
  and and_3 (and_3_out, in_5, not_4_out);
  and and_4 (and_4_out, not_5_out, not_6_out);
  and and_5 (and_5_out, and_1_out, and_2_out);
  and and_6 (and_6_out, and_3_out, and_4_out);
  and and_7 (and_7_out, and_5_out, and_6_out);
  and and_8 (out_10, and_7_out, Clk);

  // Notes on the sheet:
  //   221250'40' -> 00101000
endmodule

module P8 (
  input  in_1,
  input  in_2,
  input  in_3,
  input  in_4,
  input  in_5,
  input  in_6,
  input  in_7,
  input  in_8,
  input  in_9,
  input  in_10,
  input  in_11,
  input  in_12,
  input  in_13,
  input  in_14,
  input  in_15,
  output out_16,
  output out_17
);

  wire xor_1_out, xor_2_out, xor_3_out, xor_4_out, xor_5_out, xor_6_out, xor_7_out, xor_8_out, xor_9_out,
       xor_10_out, xor_11_out, xor_12_out;

  xor xor_1 (xor_1_out, in_1, in_2);
  xor xor_2 (xor_2_out, in_3, in_4);
  xor xor_3 (xor_3_out, in_5, in_6);
  xor xor_4 (xor_4_out, in_8, in_9);
  xor xor_5 (xor_5_out, in_10, in_11);
  xor xor_6 (xor_6_out, in_12, in_13);
  xor xor_7 (xor_7_out, in_14, in_15);
  xor xor_8 (xor_8_out, xor_1_out, xor_2_out);
  xor xor_9 (xor_9_out, xor_3_out, in_7);
  xor xor_10 (xor_10_out, xor_4_out, xor_5_out);
  xor xor_11 (xor_11_out, xor_6_out, xor_7_out);
  xor xor_12 (xor_12_out, xor_10_out, xor_11_out);
  xor xor_13 (out_16, xor_8_out, xor_9_out);
  not not_1 (out_17, xor_12_out);

  // Notes on the sheet:
  //   Find bit parity
  //   Check Parity
  //   2212504'0' -> even
endmodule
