// Logisim project Lab2.circ as structural Verilog: 6 circuits, main circuit P1
module P1 (
  input  in_1,
  input  in_2,
  input  in_3,
  input  in_4,
  input  in_5,
  input  in_6,
  output out_7,
  output out_8,
  output out_9,
  output out_10,
  output out_11,
  output out_12,
  output out_13,
  output out_14
);

  wire clock_1_out, clock_2_out, clock_3_out, clock_4_out;

  Clock clock_1 (.out(clock_1_out));
  Clock clock_2 (.out(clock_2_out));
  Clock clock_3 (.out(clock_3_out));
  Clock clock_4 (.out(clock_4_out));
  S_R_Flip_Flop s_r_ff_1 (.S(in_1), .R(in_2), .clk(clock_1_out), .Q(out_7), .Qn(out_8));  // open: reset, preset
  J_K_Flip_Flop j_k_ff_1 (.J(in_3), .K(in_4), .clk(clock_2_out), .Q(out_9), .Qn(out_10));  // open: preset, reset
  T_Flip_Flop t_ff_1 (.T(in_5), .clk(clock_3_out), .Q(out_11), .Qn(out_12));  // open: reset, preset
  D_Flip_Flop d_ff_1 (.D(in_6), .clk(clock_4_out), .Q(out_13), .Qn(out_14));  // open: preset, reset

  // Notes on the sheet:
  //   Ck
  //   0
  //   1
  //   1
  //   1
  //   1
  //   Ck
  //   0
  //   1
  //   1
  //   1
  //   1
  //   T - FF
  //   Ck
  //   0
  //   1
  //   1
  //   Ck
  //   0
  //   1
  //   1
  //   SR - FF
  //   S
  //   R
  //   x
  //   x
  //   0
  //   0
  //   0
  //   1
  //   1
  //   0
  //   1
  //   1
  //   JK - FF
  //   S
  //   R
  //   x
  //   x
  //   0
  //   0
  //   0
  //   1
  //   1
  //   0
  //   1
  //   1
  //   T
  //   x
  //   0
  //   1
  //   D - FF
  //   T
  //   x
  //   0
  //   1
  //   Q
  //   Q
  //   Q
  //   0
  //   1
  //   1
  //   Q
  //   Q
  //   Q
  //   0
  //   1
  //   ~Q
  //   Q
  //   Q
  //   Q
  //   ~Q
  //   Q
  //   Q
  //   Q
  //   ~Q
  //   ~Q
  //   ~Q
  //   ~Q
  //   1
  //   0
  //   1
  //   ~Q
  //   ~Q
  //   ~Q
  //   1
  //   0
  //   Q
  //   ~Q
  //   ~Q
  //   ~Q
  //   Q
  //   ~Q
  //   ~Q
  //   ~Q
  //   Q
  //   No Change
  //   No Change
  //   Reset -> 0
  //   Set -> 1
  //   Undefined
  //   No Change
  //   No Change
  //   Reset -> 0
  //   Set -> 1
  //   Toggle
  //   No Change
  //   No Change
  //   Toggle
  //   No Change
  //   Reset
  //   Set
endmodule

module P2 (
  output Q1,
  output Q2,
  output Q3,
  output Q4
);

  wire clock_1_out, d_ff_1_qn, d_ff_2_qn, d_ff_3_qn, d_ff_4_qn;

  Clock clock_1 (.out(clock_1_out));
  D_Flip_Flop d_ff_1 (.D(d_ff_1_qn), .clk(clock_1_out), .Q(Q1), .Qn(d_ff_1_qn));  // open: preset, reset
  // Digital_Oscilloscope digital_oscilloscope_1: pin names not known; wires that end beside it: clock_1_out, Q1, Q2, Q3, Q4
  D_Flip_Flop d_ff_2 (.D(d_ff_2_qn), .clk(d_ff_1_qn), .Q(Q2), .Qn(d_ff_2_qn));  // open: preset, reset
  Hex_Digit_Display hex_digit_display_1 (.value({Q4, Q3, Q2, Q1}));  // open: dp
  D_Flip_Flop d_ff_3 (.D(d_ff_3_qn), .clk(d_ff_2_qn), .Q(Q3), .Qn(d_ff_3_qn));  // open: preset, reset
  D_Flip_Flop d_ff_4 (.D(d_ff_4_qn), .clk(d_ff_3_qn), .Q(Q4), .Qn(d_ff_4_qn));  // open: preset, reset
endmodule

module P3 (
  output Q1,
  output Q2,
  output Q3,
  output Q4
);

  wire and_1_out, clock_1_out, j_k_ff_1_qn, j_k_ff_2_qn, j_k_ff_3_qn;

  Clock clock_1 (.out(clock_1_out));
  J_K_Flip_Flop j_k_ff_1 (
    .J(1'b1), .K(1'b1), .clk(clock_1_out), .Q(Q1), .Qn(j_k_ff_1_qn), .reset(and_1_out));  // open: preset
  J_K_Flip_Flop j_k_ff_2 (
    .J(1'b1), .K(1'b1), .clk(j_k_ff_1_qn), .Q(Q2), .Qn(j_k_ff_2_qn), .reset(and_1_out));  // open: preset
  J_K_Flip_Flop j_k_ff_3 (
    .J(1'b1), .K(1'b1), .clk(j_k_ff_2_qn), .Q(Q3), .Qn(j_k_ff_3_qn), .reset(and_1_out));  // open: preset
  J_K_Flip_Flop j_k_ff_4 (.J(1'b1), .K(1'b1), .clk(j_k_ff_3_qn), .Q(Q4), .reset(and_1_out));  // open: Qn, preset
  and and_1 (and_1_out, Q1, Q3, Q4, clock_1_out);
  // Digital_Oscilloscope digital_oscilloscope_1: pin names not known; wires that end beside it: clock_1_out, Q1, Q2, Q3, Q4, and_1_out
  Hex_Digit_Display hex_digit_display_1 (.value({Q4, Q3, Q2, Q1}));  // open: dp
endmodule

module P4 (
  input  in_1,
  output out_2,
  output out_3,
  output out_4
);

  wire and_1_out, and_2_out, clock_1_out, d_ff_3_qn;

  Clock clock_1 (.out(clock_1_out));
  Hex_Digit_Display hex_digit_display_1 (.value({in_1, out_4, out_3, out_2}));  // open: dp
  and and_1 (and_1_out, d_ff_3_qn, out_3);
  D_Flip_Flop d_ff_1 (.D(and_1_out), .clk(clock_1_out), .Q(out_2));  // open: Qn, preset, reset
  D_Flip_Flop d_ff_2 (.D(d_ff_3_qn), .clk(clock_1_out), .Q(out_3));  // open: Qn, preset, reset
  and and_2 (and_2_out, d_ff_3_qn, out_2);
  D_Flip_Flop d_ff_3 (.D(and_2_out), .clk(clock_1_out), .Q(out_4), .Qn(d_ff_3_qn));  // open: preset, reset
  // Digital_Oscilloscope digital_oscilloscope_1: pin names not known; wires that end beside it: clock_1_out, out_2, out_3, out_4
endmodule

module P5 (
  input  in_1,
  input  in_2,
  output out_3,
  output out_4,
  output out_5
);

  wire and_1_out, and_2_out, clock_1_out, nand_1_out, nor_1_out, not_1_out, not_2_out, not_3_out, not_4_out,
       or_1_out, Q1_qn, Q3_qn, xnor_1_out, xor_1_out;

  Clock clock_1 (.out(clock_1_out));
  xnor xnor_1 (xnor_1_out, in_2, out_4, out_5);
  J_K_Flip_Flop Q1 (.J(xnor_1_out), .K(not_1_out), .clk(clock_1_out), .Q(out_3), .Qn(Q1_qn));  // open: preset, reset
  not not_1 (not_1_out, xnor_1_out);
  Hex_Digit_Display hex_digit_display_1 (.value({in_1, out_5, out_4, out_3}));  // open: dp
  not not_2 (not_2_out, in_2);
  nand nand_1 (nand_1_out, not_2_out, Q1_qn, out_4);
  and and_1 (and_1_out, in_2, out_5);
  xor xor_1 (xor_1_out, and_1_out, nand_1_out);
  J_K_Flip_Flop Q2 (.J(xor_1_out), .K(not_3_out), .clk(clock_1_out), .Q(out_4));  // open: Qn, preset, reset
  not not_3 (not_3_out, xor_1_out);
  and and_2 (and_2_out, Q3_qn, in_2, out_3, out_4);
  nor nor_1 (nor_1_out, out_4, in_2, out_3);
  or or_1 (or_1_out, nor_1_out, and_2_out);
  J_K_Flip_Flop Q3 (.J(or_1_out), .K(not_4_out), .clk(clock_1_out), .Q(out_5), .Qn(Q3_qn));  // open: preset, reset
  not not_4 (not_4_out, or_1_out);
  // Digital_Oscilloscope digital_oscilloscope_1: pin names not known; wires that end beside it: clock_1_out, out_3, out_4, out_5
endmodule

module P6 (
);

  wire and_1_out, and_2_out, and_3_out, and_4_out, and_5_out, and_6_out, clock_1_out, or_1_out;
  wire [3:0] counter_1_q, counter_2_q, counter_3_q, counter_4_q, counter_5_q, counter_6_q;

  Clock clock_1 (.out(clock_1_out));
  and and_1 (and_1_out, clock_1_out, counter_1_q[3], counter_1_q[1]);
  and and_2 (and_2_out, clock_1_out, counter_2_q[2], counter_2_q[1]);
  and and_3 (and_3_out, clock_1_out, counter_3_q[3], counter_3_q[1]);
  and and_4 (and_4_out, clock_1_out, counter_4_q[2], counter_4_q[1]);
  and and_5 (and_5_out, counter_5_q[3], counter_5_q[1], clock_1_out);
  and and_6 (and_6_out, clock_1_out, counter_5_q[2], counter_6_q[1]);
  or or_1 (or_1_out, and_6_out, and_5_out);
  Counter #(.max('hf), .width(4)) counter_1 (
    .clr(and_1_out), .up(1'b1), .clk(clock_1_out), .Q(counter_1_q));  // open: load, count, D, carry
  Counter #(.max('hf), .width(4)) counter_2 (
    .clr(and_2_out), .up(1'b1), .clk(and_1_out), .Q(counter_2_q));  // open: load, count, D, carry
  Counter #(.max('hf), .width(4)) counter_3 (
    .clr(and_3_out), .up(1'b1), .clk(and_2_out), .Q(counter_3_q));  // open: load, count, D, carry
  Counter #(.max('hf), .width(4)) counter_4 (
    .clr(and_4_out), .up(1'b1), .clk(and_3_out), .Q(counter_4_q));  // open: load, count, D, carry
  Counter #(.max('hf), .width(4)) counter_5 (
    .clr(or_1_out), .up(1'b1), .clk(and_4_out), .Q(counter_5_q));  // open: load, count, D, carry
  Counter #(.max('hf), .width(4)) counter_6 (
    .clr(and_6_out), .up(1'b1), .clk(and_5_out), .Q(counter_6_q));  // open: load, count, D, carry
  Hex_Digit_Display hex_digit_display_1 (.value(counter_6_q));  // open: dp
  Hex_Digit_Display hex_digit_display_2 (.value(counter_5_q));  // open: dp
  Hex_Digit_Display hex_digit_display_3 (.value(counter_4_q));  // open: dp
  Hex_Digit_Display hex_digit_display_4 (.value(counter_3_q));  // open: dp
  Hex_Digit_Display hex_digit_display_5 (.value(counter_2_q));  // open: dp
  Hex_Digit_Display hex_digit_display_6 (.value(counter_1_q));  // open: dp
endmodule
