// Logisim project P1.circ as structural Verilog: 8 circuits, main circuit main
module main (
  input  D,
  input  C,
  input  B,
  input  A
);

  wire leda_1_out_5, ledb_1_out_5, ledc_1_e, ledd_1_out_5, lede_1_out_5, ledf_1_f, ledg_1_g;

  LedA leda_1 (.A(D), .B(C), .C(B), .D(A), .out_5(leda_1_out_5));
  LedB ledb_1 (.A(D), .B(C), .C(B), .D(A), .out_5(ledb_1_out_5));
  LedC ledc_1 (.A(D), .B(C), .C(B), .D(A), .e(ledc_1_e));
  LedD ledd_1 (.A(D), .B(C), .C(B), .D(A), .out_5(ledd_1_out_5));
  LedE lede_1 (.A(D), .B(C), .C(B), .D(A), .out_5(lede_1_out_5));
  LedF ledf_1 (.A(D), .B(C), .C(B), .D(A), .f(ledf_1_f));
  _7_Segment_Display u_7_segment_display_1 (
    .g(ledg_1_g), .f(ledf_1_f), .a(leda_1_out_5), .b(ledb_1_out_5), .e(lede_1_out_5), .d(ledd_1_out_5),
    .c(ledc_1_e));  // open: dp
  LedG ledg_1 (.A(D), .B(C), .C(B), .D(A), .g(ledg_1_g));
endmodule

module LedA (
  input  A,
  input  B,
  input  C,
  input  D,
  output out_5
);

  wire and_1_out, and_2_out, and_3_out, and_4_out, and_5_out, and_6_out, and_7_out, and_8_out, not_1_out,
       not_2_out, not_3_out, not_4_out, or_1_out, or_2_out, or_3_out, or_4_out;

  not not_1 (not_1_out, A);
  not not_2 (not_2_out, B);
  not not_3 (not_3_out, C);
  not not_4 (not_4_out, D);
  and and_1 (and_1_out, A, not_2_out);
  and and_2 (and_2_out, not_2_out, not_4_out);
  and and_3 (and_3_out, not_1_out, C);
  and and_4 (and_4_out, not_1_out, B);
  and and_5 (and_5_out, and_1_out, not_3_out);
  and and_6 (and_6_out, A, not_4_out);
  or or_1 (or_1_out, and_2_out, and_3_out);
  or or_2 (or_2_out, or_1_out, and_7_out);
  and and_7 (and_7_out, and_4_out, D);
  or or_3 (or_3_out, and_5_out, and_6_out);
  or or_4 (or_4_out, or_3_out, and_8_out);
  and and_8 (and_8_out, B, C);
  or or_5 (out_5, or_2_out, or_4_out);

  // Notes on the sheet:
  //   f = ~B.~D + ~A.C + ~A.B.D + A.~B.~C + A.~D + B.C
endmodule

module LedB (
  input  A,
  input  B,
  input  C,
  input  D,
  output out_5
);

  wire and_1_out, and_2_out, and_3_out, and_4_out, and_5_out, and_6_out, and_7_out, and_8_out, not_1_out,
       not_2_out, not_3_out, not_4_out, or_1_out, or_2_out, or_3_out;

  not not_1 (not_1_out, A);
  not not_2 (not_2_out, B);
  not not_3 (not_3_out, C);
  not not_4 (not_4_out, D);
  and and_1 (and_1_out, not_1_out, not_3_out);
  and and_2 (and_2_out, not_1_out, C);
  and and_3 (and_3_out, and_1_out, not_4_out);
  and and_4 (and_4_out, and_2_out, D);
  and and_5 (and_5_out, A, not_3_out);
  or or_1 (or_1_out, and_3_out, and_4_out);
  or or_2 (or_2_out, or_1_out, and_6_out);
  and and_6 (and_6_out, not_2_out, not_4_out);
  and and_7 (and_7_out, and_5_out, D);
  or or_3 (or_3_out, and_7_out, and_8_out);
  and and_8 (and_8_out, not_1_out, not_2_out);
  or or_4 (out_5, or_2_out, or_3_out);

  // Notes on the sheet:
  //   f = ~A.~C.~D + ~A.C.D + ~B.~D + A.~C.D + ~A.~B
endmodule

module LedC (
  input  A,
  input  B,
  input  C,
  input  D,
  output e
);

  wire and_1_out, and_2_out, and_3_out, and_4_out, and_5_out, not_1_out, not_2_out, not_3_out, or_1_out,
       or_2_out, or_4_out;

  not not_1 (not_1_out, A);
  not not_2 (not_2_out, B);
  not not_3 (not_3_out, C);
  and and_1 (and_1_out, not_1_out, B);
  and and_2 (and_2_out, A, not_2_out);
  or or_1 (or_1_out, and_1_out, and_2_out);
  and and_3 (and_3_out, not_3_out, D);
  and and_4 (and_4_out, not_1_out, not_3_out);
  and and_5 (and_5_out, not_1_out, D);
  or or_2 (or_2_out, or_1_out, and_3_out);
  or or_3 (e, or_2_out, or_4_out);
  or or_4 (or_4_out, and_4_out, and_5_out);

  // Notes on the sheet:
  //   f = ~A.B + A.~B + ~C.D + ~A.~C + ~A.D
endmodule

module LedD (
  input  A,
  input  B,
  input  C,
  input  D,
  output out_5
);

  wire and_1_out, and_2_out, and_3_out, and_4_out, and_5_out, and_6_out, and_7_out, and_8_out, and_9_out,
       and_10_out, and_11_out, and_12_out, and_13_out, and_14_out, and_15_out, not_1_out, not_2_out,
       not_3_out, not_4_out, or_1_out, or_2_out, or_3_out, or_4_out, or_5_out, or_6_out;

  not not_1 (not_1_out, A);
  not not_2 (not_2_out, B);
  not not_3 (not_3_out, C);
  not not_4 (not_4_out, D);
  and and_1 (and_1_out, B, not_3_out);
  and and_2 (and_2_out, not_1_out, not_2_out);
  and and_3 (and_3_out, not_1_out, not_2_out);
  and and_4 (and_4_out, not_1_out, C);
  and and_5 (and_5_out, not_2_out, not_3_out);
  and and_6 (and_6_out, A, not_2_out);
  and and_7 (and_7_out, B, C);
  and and_8 (and_8_out, and_1_out, D);
  and and_9 (and_9_out, and_2_out, not_4_out);
  and and_10 (and_10_out, and_3_out, C);
  and and_11 (and_11_out, and_4_out, not_4_out);
  and and_12 (and_12_out, and_5_out, not_4_out);
  and and_13 (and_13_out, and_6_out, D);
  and and_14 (and_14_out, A, not_3_out);
  and and_15 (and_15_out, and_7_out, not_4_out);
  or or_1 (or_1_out, and_8_out, and_9_out);
  or or_2 (or_2_out, or_1_out, or_3_out);
  or or_3 (or_3_out, and_10_out, and_11_out);
  or or_4 (or_4_out, and_12_out, and_13_out);
  or or_5 (or_5_out, or_4_out, or_6_out);
  or or_6 (or_6_out, and_14_out, and_15_out);
  or or_7 (out_5, or_2_out, or_5_out);

  // Notes on the sheet:
  //   f = B.~C.D + ~A.~B.~D + ~A.~B.C + ~A.C.~D + ~B.~C.~D + A.~B.D + A.~C + B.C.~D
endmodule

module LedE (
  input  A,
  input  B,
  input  C,
  input  D,
  output out_5
);

  wire and_1_out, and_2_out, and_3_out, and_4_out, not_1_out, not_2_out, or_1_out, or_2_out;

  not not_1 (not_1_out, B);
  not not_2 (not_2_out, D);
  and and_1 (and_1_out, not_1_out, not_2_out);
  and and_2 (and_2_out, C, not_2_out);
  and and_3 (and_3_out, A, C);
  and and_4 (and_4_out, A, B);
  or or_1 (or_1_out, and_1_out, and_2_out);
  or or_2 (or_2_out, and_3_out, and_4_out);
  or or_3 (out_5, or_1_out, or_2_out);

  // Notes on the sheet:
  //   f = ~B.~D + C.~D + A.C + A.B
endmodule

module LedF (
  input  A,
  input  B,
  input  C,
  input  D,
  output f
);

  wire and_1_out, and_2_out, and_3_out, and_4_out, and_5_out, and_6_out, not_1_out, not_2_out, not_3_out,
       not_4_out, or_1_out, or_2_out, or_3_out;

  not not_1 (not_1_out, A);
  not not_2 (not_2_out, B);
  not not_3 (not_3_out, C);
  not not_4 (not_4_out, D);
  and and_1 (and_1_out, not_1_out, B);
  and and_2 (and_2_out, not_3_out, not_4_out);
  and and_3 (and_3_out, and_1_out, not_3_out);
  or or_1 (or_1_out, and_2_out, and_3_out);
  or or_2 (or_2_out, or_1_out, and_4_out);
  and and_4 (and_4_out, B, not_4_out);
  and and_5 (and_5_out, A, not_2_out);
  or or_3 (or_3_out, and_5_out, and_6_out);
  and and_6 (and_6_out, A, C);
  or or_4 (f, or_2_out, or_3_out);

  // Notes on the sheet:
  //   f = ~C.~D + ~A.B.~C + B.~D + A.~B + A.C
endmodule

module LedG (
  input  A,
  input  B,
  input  C,
  input  D,
  output g
);

  wire and_1_out, and_2_out, and_3_out, and_4_out, and_5_out, and_6_out, and_7_out, and_8_out, and_9_out,
       and_10_out, not_1_out, not_2_out, not_3_out, not_4_out, or_1_out, or_2_out, or_3_out, or_4_out,
       or_5_out;

  not not_1 (not_1_out, A);
  not not_2 (not_2_out, B);
  not not_3 (not_3_out, C);
  not not_4 (not_4_out, D);
  and and_1 (and_1_out, not_1_out, B);
  and and_2 (and_2_out, not_1_out, B);
  and and_3 (and_3_out, B, not_3_out);
  and and_4 (and_4_out, not_2_out, C);
  and and_5 (and_5_out, A, not_2_out);
  and and_6 (and_6_out, and_1_out, not_3_out);
  and and_7 (and_7_out, and_2_out, not_4_out);
  and and_8 (and_8_out, and_3_out, D);
  and and_9 (and_9_out, C, not_4_out);
  or or_1 (or_1_out, and_4_out, and_5_out);
  or or_2 (or_2_out, or_1_out, or_3_out);
  or or_3 (or_3_out, and_6_out, and_7_out);
  or or_4 (or_4_out, and_8_out, and_9_out);
  or or_5 (or_5_out, or_4_out, and_10_out);
  and and_10 (and_10_out, A, D);
  or or_6 (g, or_2_out, or_5_out);

  // Notes on the sheet:
  //   f = ~B.C + A.~B + . A.B.~C + ~A.B.~D + B.~C.D + C.~D + A.D
endmodule
