// Logisim project P2.circ as structural Verilog: 8 circuits, main circuit main
module main (
  input  in_1,
  input  in_2,
  input  in_3,
  input  in_4
);

  wire leda_1_e, ledb_1_f, ledc_1_g, ledd_1_h, lede_1_k, ledf_1_j, ledg_1_m;

  LedA leda_1 (.A(in_1), .B(in_2), .C(in_3), .D(in_4), .e(leda_1_e));
  LedB ledb_1 (.A(in_1), .B(in_2), .C(in_3), .D(in_4), .f(ledb_1_f));
  LedC ledc_1 (.A(in_1), .B(in_2), .C(in_3), .D(in_4), .g(ledc_1_g));
  LedD ledd_1 (.A(in_1), .B(in_2), .C(in_3), .D(in_4), .h(ledd_1_h));
  LedE lede_1 (.A(in_1), .B(in_2), .C(in_3), .D(in_4), .k(lede_1_k));
  LedF ledf_1 (.A(in_1), .B(in_2), .C(in_3), .D(in_4), .j(ledf_1_j));
  _7_Segment_Display #(.active("false")) u_7_segment_display_1 (
    .g(ledg_1_m), .f(ledf_1_j), .a(leda_1_e), .b(ledb_1_f), .e(lede_1_k), .d(ledd_1_h), .c(ledc_1_g));  // open: dp
  LedG ledg_1 (.A(in_1), .B(in_2), .C(in_3), .D(in_4), .m(ledg_1_m));

  // Notes on the sheet:
  //   D
  //   C
  //   B
  //   A
endmodule

module LedA (
  input  A,
  input  B,
  input  C,
  input  D,
  output e
);

  wire and_1_out, and_2_out, and_3_out, and_4_out, and_5_out, and_6_out, and_7_out, and_8_out, and_9_out,
       and_10_out, and_11_out, and_12_out, not_1_out, not_2_out, not_3_out, not_4_out, or_1_out, or_3_out;

  not not_1 (not_1_out, A);
  not not_2 (not_2_out, B);
  not not_3 (not_3_out, C);
  not not_4 (not_4_out, D);
  and and_1 (and_1_out, not_1_out, not_2_out);
  and and_2 (and_2_out, not_3_out, D);
  and and_3 (and_3_out, not_1_out, B);
  and and_4 (and_4_out, not_3_out, not_4_out);
  and and_5 (and_5_out, A, not_2_out);
  and and_6 (and_6_out, C, D);
  and and_7 (and_7_out, A, B);
  and and_8 (and_8_out, not_3_out, D);
  and and_9 (and_9_out, and_1_out, and_2_out);
  and and_10 (and_10_out, and_3_out, and_4_out);
  and and_11 (and_11_out, and_5_out, and_6_out);
  and and_12 (and_12_out, and_7_out, and_8_out);
  or or_1 (or_1_out, and_9_out, and_10_out);
  or or_2 (e, or_1_out, or_3_out);
  or or_3 (or_3_out, and_11_out, and_12_out);

  // Notes on the sheet:
  //   f = ~A⋅~B⋅~C⋅D+~A⋅B⋅~C⋅~D+A⋅~B⋅C⋅D+A⋅B⋅~C⋅D
endmodule

module LedB (
  input  A,
  input  B,
  input  C,
  input  D,
  output f
);

  wire and_1_out, and_2_out, and_3_out, and_4_out, and_5_out, and_6_out, and_7_out, and_8_out, and_9_out,
       not_1_out, not_2_out, not_3_out, or_1_out, or_3_out;

  not not_1 (not_1_out, A);
  not not_2 (not_2_out, C);
  not not_3 (not_3_out, D);
  and and_1 (and_1_out, not_1_out, B);
  and and_2 (and_2_out, not_2_out, D);
  and and_3 (and_3_out, B, C);
  and and_4 (and_4_out, A, C);
  and and_5 (and_5_out, A, B);
  and and_6 (and_6_out, and_1_out, and_2_out);
  and and_7 (and_7_out, and_3_out, not_3_out);
  and and_8 (and_8_out, and_4_out, D);
  and and_9 (and_9_out, and_5_out, not_3_out);
  or or_1 (or_1_out, and_6_out, and_7_out);
  or or_2 (f, or_1_out, or_3_out);
  or or_3 (or_3_out, and_8_out, and_9_out);

  // Notes on the sheet:
  //   f = ~A⋅B⋅~C⋅D+B⋅C⋅~D+A⋅C⋅D+A⋅B⋅~D
endmodule

module LedC (
  input  A,
  input  B,
  input  C,
  input  D,
  output g
);

  wire and_1_out, and_2_out, and_3_out, and_4_out, and_5_out, and_6_out, and_7_out, not_1_out, not_2_out,
       not_3_out, or_1_out;

  not not_1 (not_1_out, A);
  not not_2 (not_2_out, B);
  not not_3 (not_3_out, D);
  and and_1 (and_1_out, not_1_out, not_2_out);
  and and_2 (and_2_out, C, not_3_out);
  and and_3 (and_3_out, A, B);
  and and_4 (and_4_out, and_1_out, and_2_out);
  and and_5 (and_5_out, and_3_out, not_3_out);
  and and_6 (and_6_out, A, B);
  or or_1 (or_1_out, and_4_out, and_5_out);
  or or_2 (g, or_1_out, and_7_out);
  and and_7 (and_7_out, and_6_out, C);

  // Notes on the sheet:
  //   f = ~A⋅~B⋅C⋅~D+A⋅B⋅~D+A⋅B⋅C
endmodule

module LedD (
  input  A,
  input  B,
  input  C,
  input  D,
  output h
);

  wire and_1_out, and_2_out, and_3_out, and_4_out, and_5_out, and_6_out, and_7_out, and_8_out, and_9_out,
       and_10_out, and_11_out, not_1_out, not_2_out, not_3_out, not_4_out, or_1_out, or_3_out;

  not not_1 (not_1_out, A);
  not not_2 (not_2_out, B);
  not not_3 (not_3_out, C);
  not not_4 (not_4_out, D);
  and and_1 (and_1_out, not_1_out, not_2_out);
  and and_2 (and_2_out, not_3_out, D);
  and and_3 (and_3_out, not_1_out, B);
  and and_4 (and_4_out, not_3_out, not_4_out);
  and and_5 (and_5_out, B, C);
  and and_6 (and_6_out, A, not_2_out);
  and and_7 (and_7_out, C, not_4_out);
  and and_8 (and_8_out, and_1_out, and_2_out);
  and and_9 (and_9_out, and_3_out, and_4_out);
  and and_10 (and_10_out, and_5_out, D);
  and and_11 (and_11_out, and_6_out, and_7_out);
  or or_1 (or_1_out, and_8_out, and_9_out);
  or or_2 (h, or_1_out, or_3_out);
  or or_3 (or_3_out, and_10_out, and_11_out);

  // Notes on the sheet:
  //   f = ~A⋅~B⋅~C⋅D+~A⋅B⋅~C⋅~D+B⋅C⋅D+A⋅~B⋅C⋅~D
endmodule

module LedE (
  input  A,
  input  B,
  input  C,
  input  D,
  output k
);

  wire and_1_out, and_2_out, and_3_out, and_4_out, and_5_out, not_1_out, not_2_out, not_3_out, or_1_out;

  not not_1 (not_1_out, A);
  not not_2 (not_2_out, B);
  not not_3 (not_3_out, C);
  and and_1 (and_1_out, not_1_out, B);
  and and_2 (and_2_out, not_1_out, D);
  and and_3 (and_3_out, and_1_out, not_3_out);
  and and_4 (and_4_out, not_2_out, not_3_out);
  or or_1 (or_1_out, and_2_out, and_3_out);
  or or_2 (k, or_1_out, and_5_out);
  and and_5 (and_5_out, and_4_out, D);

  // Notes on the sheet:
  //   f = ~A⋅D+~A⋅B⋅~C+~B⋅~C⋅D
endmodule

module LedF (
  input  A,
  input  B,
  input  C,
  input  D,
  output j
);

  wire and_1_out, and_2_out, and_3_out, and_4_out, and_5_out, and_6_out, and_7_out, and_8_out, and_9_out,
       not_1_out, not_2_out, not_3_out, or_1_out, or_3_out;

  not not_1 (not_1_out, A);
  not not_2 (not_2_out, B);
  not not_3 (not_3_out, C);
  and and_1 (and_1_out, not_1_out, not_2_out);
  and and_2 (and_2_out, not_1_out, not_2_out);
  and and_3 (and_3_out, not_1_out, C);
  and and_4 (and_4_out, A, B);
  and and_5 (and_5_out, not_3_out, D);
  and and_6 (and_6_out, and_1_out, D);
  and and_7 (and_7_out, and_2_out, C);
  and and_8 (and_8_out, and_3_out, D);
  and and_9 (and_9_out, and_4_out, and_5_out);
  or or_1 (or_1_out, and_6_out, and_7_out);
  or or_2 (j, or_1_out, or_3_out);
  or or_3 (or_3_out, and_8_out, and_9_out);

  // Notes on the sheet:
  //   f = ~A⋅~B⋅D+~A⋅~B⋅C+~A⋅C⋅D+A⋅B⋅~C⋅D
endmodule

module LedG (
  input  A,
  input  B,
  input  C,
  input  D,
  output m
);

  wire and_1_out, and_2_out, and_3_out, and_4_out, and_5_out, and_6_out, and_7_out, and_8_out, not_1_out,
       not_2_out, not_3_out, not_4_out, or_1_out;

  not not_1 (not_1_out, A);
  not not_2 (not_2_out, B);
  not not_3 (not_3_out, C);
  not not_4 (not_4_out, D);
  and and_1 (and_1_out, not_1_out, not_2_out);
  and and_2 (and_2_out, not_1_out, B);
  and and_3 (and_3_out, C, D);
  and and_4 (and_4_out, and_1_out, not_3_out);
  and and_5 (and_5_out, and_2_out, and_3_out);
  and and_6 (and_6_out, A, B);
  and and_7 (and_7_out, not_3_out, not_4_out);
  or or_1 (or_1_out, and_4_out, and_5_out);
  or or_2 (m, or_1_out, and_8_out);
  and and_8 (and_8_out, and_6_out, and_7_out);

  // Notes on the sheet:
  //   f = ~A⋅~B⋅~C+~A⋅B⋅C⋅D+A⋅B⋅~C⋅~D
endmodule
