// Logisim project P3.circ as structural Verilog: 1 circuit, main circuit main
module main (
  input  I_3,
  input  I_2,
  input  I_1,
  input  I_0,
  output O_0,
  output O_1,
  output v
);

  wire and_1_out, not_1_out;

  not not_1 (not_1_out, I_2);
  or or_1 (O_1, I_3, I_2);
  and and_1 (and_1_out, not_1_out, I_1);
  or or_2 (O_0, I_3, and_1_out);
  or or_3 (v, O_1, I_1, I_0);
endmodule
