// Logisim project P5.circ as structural Verilog: 1 circuit, main circuit main
module main (
  input  I0,
  input  I1,
  input  I2,
  input  I3,
  input  in_5,
  input  in_6,
  output out_7
);

  wire multiplexer_1_out, multiplexer_2_out;

  Multiplexer multiplexer_1 (.in0(I0), .in1(I1), .out(multiplexer_1_out), .sel(in_5));
  Multiplexer multiplexer_2 (.in0(I2), .in1(I3), .out(multiplexer_2_out), .sel(in_5));
  Multiplexer multiplexer_3 (.in0(multiplexer_1_out), .in1(multiplexer_2_out), .out(out_7), .sel(in_6));

  // Notes on the sheet:
  //   S1
  //   S0
endmodule
