// Logisim project P6.circ as structural Verilog: 3 circuits, main circuit main
module main (
  input  [1:0] in_1,
  input  in_2,
  input  in_3,
  input  in_4,
  input  in_5,
  input  in_6,
  input  in_7,
  input  in_8,
  input  in_9,
  input  in_10,
  input  D,
  input  S2,
  input  [1:0] S13,
  output out_14,
  output out_15,
  output out_16,
  output out_17,
  output out_18,
  output out_19,
  output out_20,
  output out_21,
  output out_22
);

  wire multiplexer_1_out, multiplexer_2_out, not_1_out;

  not not_1 (not_1_out, S2);
  Multiplexer #(.select(2)) multiplexer_1 (
    .in0(in_3), .in1(in_4), .in2(in_5), .in3(in_6), .out(multiplexer_1_out), .sel(in_1));
  Multiplexer #(.select(2)) multiplexer_2 (
    .in0(in_7), .in1(in_8), .in2(in_9), .in3(in_10), .out(multiplexer_2_out), .sel(in_1));
  Demultiplexer #(.enable("true"), .select(2)) demultiplexer_1 (
    .out0(out_15), .out1(out_16), .out2(out_17), .out3(out_18), .in(D), .sel(S13), .en(not_1_out));
  Demultiplexer #(.enable("true"), .select(2)) demultiplexer_2 (
    .out0(out_19), .out1(out_20), .out2(out_21), .out3(out_22), .in(D), .sel(S13), .en(S2));
  Multiplexer multiplexer_3 (.in0(multiplexer_1_out), .in1(multiplexer_2_out), .out(out_14), .sel(in_2));

  // Notes on the sheet:
  //   MUX 8:1
  //   Demux 1:8
endmodule

module MUX41 (
  input  S1,
  input  I3,
  input  S0,
  input  I2,
  input  I1,
  input  I0,
  output Z0
);

  wire and_1_out, and_2_out, and_3_out, and_4_out, not_1_out, not_2_out;

  not not_1 (not_1_out, S1);
  not not_2 (not_2_out, S0);
  and and_1 (and_1_out, S1, S0, I3);
  and and_2 (and_2_out, S1, not_2_out, I2);
  and and_3 (and_3_out, not_1_out, S0, I1);
  and and_4 (and_4_out, not_2_out, not_1_out, I0);
  or or_1 (Z0, and_1_out, and_2_out, and_3_out, and_4_out);
endmodule

module Demux14 (
  input  A,
  input  B,
  input  D,
  output Z0,
  output Z1,
  output Z2,
  output Z3
);

  wire not_1_out, not_2_out;

  not not_1 (not_1_out, A);
  not not_2 (not_2_out, B);
  and and_1 (Z0, D, not_2_out, not_1_out);
  and and_2 (Z1, D, B, not_1_out);
  and and_3 (Z2, D, A, not_2_out);
  and and_4 (Z3, D, A, B);
endmodule
